// Logisim project assignmentActivityUnit01.circ as structural Verilog: 1 circuit, main circuit main
module main (
);

  wire buffer00_out, switch00_p2;

  // Switch switch00: pin names not known; wires that end beside it: 1'b1, switch00_p2
  buf buffer00 (buffer00_out, switch00_p2);
  LED led1 (.in(buffer00_out));

  // Notes on the sheet:
  //   Battery
endmodule
