// Logisim project discUni01.circ as structural Verilog: 1 circuit, main circuit main
// yes
module main (
  input  A0,
  input  B0,
  input  A1,
  input  B1,
  output Sum0,
  output C0,
  output Sum1,
  output C1
);

  wire AND01_out, AND02_out, XOR02_out;

  xor XOR01 (Sum0, A0, B0);
  xor XOR02 (XOR02_out, A1, B1);
  and AND00 (C0, A0, B0);
  and AND02 (AND02_out, A1, B1);
  xor XOR03 (Sum1, C0, XOR02_out);
  and AND01 (AND01_out, C0, XOR02_out);
  or OR00 (C1, AND01_out, AND02_out);
endmodule
