// Logisim project PLDs_ROM.circ as structural Verilog: 1 circuit, main circuit main
module main (
  input  Reset
);

  wire Clock, counter_1_carry;
  wire [3:0] binary_to_bcd_converter_1_p2, binary_to_bcd_converter_1_p3, binary_to_bcd_converter_1_p4;
  wire [6:0] rom_1_data;
  wire [7:0] counter_1_q;

  Clock clock_1 (.out(Clock));
  Counter counter_1 (.clr(Reset), .clk(Clock), .carry(counter_1_carry), .Q(counter_1_q));  // open: load, up, count, D
  LED led_1 (.in(Clock));
  LED led_2 (.in(counter_1_carry));
  ROM #(.dataWidth(7)) rom_1 (.addr(counter_1_q), .data(rom_1_data));
  // Digital_Oscilloscope digital_oscilloscope_1: pin names not known; wires that end beside it: Clock
  Hex_Digit_Display hex_digit_display_1 (.value(binary_to_bcd_converter_1_p2));  // open: dp
  // Binary_to_BCD_converter #(.binvalue(7)) binary_to_bcd_converter_1: pin names not known; wires that end beside it: rom_1_data, binary_to_bcd_converter_1_p2, binary_to_bcd_converter_1_p3, binary_to_bcd_converter_1_p4
  TTY tty_1 (.data(rom_1_data), .clk(Clock));  // open: we, clr
  Hex_Digit_Display hex_digit_display_2 (.value(binary_to_bcd_converter_1_p3));  // open: dp
  Hex_Digit_Display hex_digit_display_3 (.value(binary_to_bcd_converter_1_p4));  // open: dp

  // Notes on the sheet:
  //   MaxMemory
  //   contents of rom_1 (hex, n*v repeats v):
  //   57 65 6c 63 6f 6d 65 20 74 6f 20 55 6f 50 65 6f 70 6c 65 2c 20 74 68 65 20 75 6e 69 76 65 72 73 69
  //   74 79 20 74 68 61 74 20 77 69 6c 6c 20 6d 61 6b 65 20 79 6f 75 72 20 64 72 65 61 6d 73 20 63 6f 6d
  //   65 20 74 72 75 65 2e d a d a 42 65 20 72 65 73 69 6c 69 65 6e 74 21 d a d a 4d 61 74 65 75 73 20 4f
  //   6c 69 76 65 69 72 61 21
endmodule
